# Fritzing sketch temperature-logger (saved by Fritzing 0.7.7b)
breadboards: 1

parts:
  T1 = LM35 Temperature Sensor [package="TO92 [THT]"]
  Arduino1 = Arduino
  Part1 = OpenLog

nets:
  N1: T1.+Vs, Arduino1.+5V, Part1.DTR
  N2: T1.Vout, Arduino1.A0
  GND: T1.GND, Arduino1.GND, Part1.TXO
  N3: Arduino1.D1TX, Part1.GND

notes:
  The SDLogger has three lines: power (red), ground (black), and receive (yellow).
  The yellow wire goes into the TX (transmit) pin on the Arduino. The Arduino transmits data to the SDLogger.
  Read the temp sensor from the flat side, left to right: power, signal, ground.
  The signal line should connect to the A0 pin on the Arduino.
