# Fritzing sketch light-control-circuit (saved by Fritzing 0.7.7b)
breadboards: 1

parts:
  Arduino1 = Arduino
  LED1 = LED - 5mm [color="Green (570nm)" package="5 mm [THT]"]
  R1 = Resistor [tolerance=±5% resistance=470 package=THT]
  R2 = Photocell (LDR) [package=THT]
  R3 = Resistor [tolerance=±5% resistance=10k package=THT]

nets:
  N1: Arduino1.GND, LED1.cathode, R2.pin_1
  N2: Arduino1.D7, R1.Pin_0
  N3: Arduino1.+5V, R3.Pin_0
  N4: Arduino1.A0, R2.pin_0, R3.Pin_1
  N5: LED1.anode, R1.Pin_1
