# Fritzing sketch ldr-divider-circuit (saved by Fritzing 0.7.7b)
breadboards: 1

parts:
  Photocell = Photocell (LDR) [package=THT]
  R2 = Resistor [tolerance=±5% resistance=10k package=THT]
  Freeduino = Arduino

nets:
  N1: Photocell.pin_0, R2.Pin_1, Freeduino.A0
  N2: Photocell.pin_1, Freeduino.GND
  N3: R2.Pin_0, Freeduino.+5V
