# Fritzing sketch trim-pot-circuit (saved by Fritzing 0.7.7b)
breadboards: 1

parts:
  R2 = Resistor [tolerance=±5% resistance=10k package=THT]
  Freeduino = Arduino
  R3 = Trimmer Potentiometer [maximum_resistance=10kΩ package=THT]

nets:
  N1: R2.Pin_0, Freeduino.+5V
  N2: R2.Pin_1, R3.leg1
  N3: Freeduino.GND, Freeduino.A0, R3.wiper

notes:
  Measure resistance across these two pins.
  Unplug this red wire before
  trying to do measurements
  with your multimeter.
